# Fritzing sketch Yoon_Pj2_PCB (saved by Fritzing 0.7.10b)
breadboards: 1

parts:
  Arduino1 = Arduino
  R1 = Resistor [tolerance=±5% resistance=220 package=THT]
  R2 = Resistor [tolerance=±5% resistance=220 package=THT]
  R3 = Resistor [tolerance=±5% resistance=220 package=THT]
  LED1 = LED - 5mm [color="Red (633nm)" package="5 mm [THT]"]
  LED2 = LED - 5mm [color="Yellow (585nm)" package="5 mm [THT]"]
  LED3 = LED - 5mm [color="Green (555nm)" package="5 mm [THT]"]
  joystick = Thumb Joystick
  S3 = Round Pushbutton
  S4 = Round Pushbutton
  R5 = Resistor [tolerance=±5% resistance=1k package=THT]
  R6 = Resistor [tolerance=±5% resistance=1k package=THT]

nets:
  GND: Arduino1.GND, R1.Pin_1, R2.Pin_1, R3.Pin_1, joystick.GND, R5.Pin_1, R6.Pin_1
  N1: Arduino1.D10, S3.leg0, R5.Pin_0
  N2: Arduino1.D8, S4.leg0, R6.Pin_0
  N3: Arduino1.D6, LED3.cathode
  N4: Arduino1.D4, LED2.cathode
  N5: Arduino1.D2, LED1.cathode
  +5V: Arduino1.+5V, joystick.VCC, S3.leg1, S4.leg1
  N6: Arduino1.A0, joystick.VERT
  N7: Arduino1.A1, joystick.HORZ
  N8: R1.Pin_0, LED1.anode
  N9: R2.Pin_0, LED2.anode
  N10: R3.Pin_0, LED3.anode

notes:
  The joystick will be on top of pcb and the traces will be underneath, so it's ok if they overlap here
  I simplified a couple of things to remove jumpers and also thickened the traces.
